// Logisim project Logisim_8_bit_ALU_design.circ as structural Verilog: 2 circuits, main circuit 8bitALU
module _8bitALU (
  input  [7:0] B,
  input  [7:0] A,
  input  Cin,
  input  [4:0] F0_F1_enA_enB_invA,
  output Cout,
  output out_6,
  output out_7,
  output out_8,
  output out_9,
  output out_10,
  output out_11,
  output out_12,
  output out_13
);

  wire alu_1_carry_out, alu_3_carry_out, alu_4_carry_out, alu_5_carry_out, alu_6_carry_out, alu_7_carry_out,
       alu_8_carry_out;
  wire [4:0] alu_1_f0_f1_ena_enb_inva_2, alu_2_f0_f1_ena_enb_inva_2, alu_3_f0_f1_ena_enb_inva_2,
       alu_4_f0_f1_ena_enb_inva_2, alu_5_f0_f1_ena_enb_inva_2, alu_6_f0_f1_ena_enb_inva_2,
       alu_7_f0_f1_ena_enb_inva_2;

  ALU alu_1 (
    .Carry_out(alu_1_carry_out), .F0_F1_enA_enB_invA(alu_2_f0_f1_ena_enb_inva_2), .A(A[6]), .B(B[6]),
    .C_out(out_7), .Carry_in(alu_3_carry_out), .F0_F1_enA_enB_invA_2(alu_1_f0_f1_ena_enb_inva_2));
  ALU alu_2 (
    .Carry_out(Cout), .F0_F1_enA_enB_invA(F0_F1_enA_enB_invA), .A(A[7]), .B(B[7]), .C_out(out_6),
    .Carry_in(alu_1_carry_out), .F0_F1_enA_enB_invA_2(alu_2_f0_f1_ena_enb_inva_2));
  ALU alu_3 (
    .Carry_out(alu_3_carry_out), .F0_F1_enA_enB_invA(alu_1_f0_f1_ena_enb_inva_2), .A(A[5]), .B(B[5]),
    .C_out(out_8), .Carry_in(alu_4_carry_out), .F0_F1_enA_enB_invA_2(alu_3_f0_f1_ena_enb_inva_2));
  ALU alu_4 (
    .Carry_out(alu_4_carry_out), .F0_F1_enA_enB_invA(alu_3_f0_f1_ena_enb_inva_2), .A(A[4]), .B(B[4]),
    .C_out(out_9), .Carry_in(alu_5_carry_out), .F0_F1_enA_enB_invA_2(alu_4_f0_f1_ena_enb_inva_2));
  ALU alu_5 (
    .Carry_out(alu_5_carry_out), .F0_F1_enA_enB_invA(alu_4_f0_f1_ena_enb_inva_2), .A(A[3]), .B(B[3]),
    .C_out(out_10), .Carry_in(alu_6_carry_out), .F0_F1_enA_enB_invA_2(alu_5_f0_f1_ena_enb_inva_2));
  ALU alu_6 (
    .Carry_out(alu_6_carry_out), .F0_F1_enA_enB_invA(alu_5_f0_f1_ena_enb_inva_2), .A(A[2]), .B(B[2]),
    .C_out(out_11), .Carry_in(alu_7_carry_out), .F0_F1_enA_enB_invA_2(alu_6_f0_f1_ena_enb_inva_2));
  ALU alu_7 (
    .Carry_out(alu_7_carry_out), .F0_F1_enA_enB_invA(alu_6_f0_f1_ena_enb_inva_2), .A(A[1]), .B(B[1]),
    .C_out(out_12), .Carry_in(alu_8_carry_out), .F0_F1_enA_enB_invA_2(alu_7_f0_f1_ena_enb_inva_2));
  ALU alu_8 (
    .Carry_out(alu_8_carry_out), .F0_F1_enA_enB_invA(alu_7_f0_f1_ena_enb_inva_2), .A(A[0]), .B(B[0]),
    .C_out(out_13), .Carry_in(Cin));  // open: F0_F1_enA_enB_invA_2

  // Notes on the sheet:
  //   F0 F1 = 00 and, 01 or, 10 not B, 11 full adder
endmodule

module ALU (
  input  [4:0] F0_F1_enA_enB_invA,
  input  Carry_in,
  input  A,
  input  B,
  output Carry_out,
  output [4:0] F0_F1_enA_enB_invA_2,
  output C_out
);

  wire and_1_out, and_2_out, and_3_out, and_4_out, and_6_out, and_7_out, and_8_out, and_9_out, and_10_out,
       not_1_out, not_2_out, not_3_out, or_1_out, or_2_out, xor_1_out, xor_2_out, xor_3_out;

  and and_1 (and_1_out, F0_F1_enA_enB_invA[2], A);
  and and_2 (and_2_out, F0_F1_enA_enB_invA[1], B);
  xor xor_1 (xor_1_out, F0_F1_enA_enB_invA[0], and_1_out);
  and and_3 (and_3_out, xor_1_out, and_2_out);
  or or_1 (or_1_out, xor_1_out, and_2_out);
  not not_1 (not_1_out, and_2_out);
  and and_4 (and_4_out, and_2_out, xor_1_out);
  or or_2 (or_2_out, and_4_out, and_6_out);
  and and_5 (Carry_out, or_2_out, F0_F1_enA_enB_invA[4], F0_F1_enA_enB_invA[3]);
  xor xor_2 (xor_2_out, xor_1_out, and_2_out);
  and and_6 (and_6_out, xor_2_out, Carry_in);
  xor xor_3 (xor_3_out, Carry_in, xor_2_out);
  not not_2 (not_2_out, F0_F1_enA_enB_invA[4]);
  not not_3 (not_3_out, F0_F1_enA_enB_invA[3]);
  and and_7 (and_7_out, not_2_out, not_3_out, and_3_out);
  and and_8 (and_8_out, not_2_out, F0_F1_enA_enB_invA[3], or_1_out);
  and and_9 (and_9_out, F0_F1_enA_enB_invA[4], not_3_out, not_1_out);
  and and_10 (and_10_out, F0_F1_enA_enB_invA[4], F0_F1_enA_enB_invA[3], xor_3_out);
  or or_3 (C_out, and_7_out, and_8_out, and_9_out, and_10_out);

  assign F0_F1_enA_enB_invA_2 = F0_F1_enA_enB_invA;

  // Notes on the sheet:
  //   F0 F1 = 00 and, 01 or, 10 not B, 11 full adder
endmodule
